# Fritzing sketch envduino (saved by Fritzing 0.8.0b)
breadboards: 2

parts:
  part = BMP085 Breakout
  part_2 = Arduino Mega
  LED1 = LED - 5mm [color="Yellow (592nm)" package="5 mm [THT]"]
  LED2 = LED - 5mm [color="Red (633nm)" package="5 mm [THT]"]
  LED3 = LED - 5mm [color="Green (560nm)" package="5 mm [THT]"]
  R2 = Resistor [tolerance=±5% resistance=330 package=THT]
  R1 = Resistor [tolerance=±5% resistance=330 package=THT]
  R3 = Resistor [tolerance=±5% resistance=330 package=THT]
  DHT1 = DHT22 Humidity and Temperature Sensor
  R2_2 = Resistor [tolerance=±5% resistance=10k package=THT]

nets:
  N1: part.SCL, part_2.D21
  N2: part.SDA, part_2.D20
  GND: part_2.GND, R2.Pin_1, R1.Pin_1, R3.Pin_1, DHT1.GND
  +5V: part_2.+5V, DHT1.VDD, R2_2.Pin_1
  N3: part_2.D22, LED3.cathode
  N4: part_2.D24, LED1.cathode
  N5: part_2.D26, LED2.cathode
  N6: part_2.D28, DHT1.DATA, R2_2.Pin_0
  N7: LED1.anode, R1.Pin_0
  N8: LED2.anode, R2.Pin_0
  N9: LED3.anode, R3.Pin_0

custom parts:
  BMP085 Breakout: A breakout for the BMP085 barometric pressure and temperature sensor
